// Logisim project Decoder 2 bits.circ as structural Verilog: 1 circuit, main circuit main
module main (
  input  [1:0] in_1
);

  wire decoder_1_out0, decoder_1_out1, decoder_1_out2, decoder_1_out3;

  Decoder #(.select(2)) decoder_1 (
    .out0(decoder_1_out0), .out1(decoder_1_out1), .out2(decoder_1_out2), .out3(decoder_1_out3), .sel(in_1),
    .en(1'b1));
  LED _0 (.in(decoder_1_out0));
  LED _1 (.in(decoder_1_out1));
  LED _2 (.in(decoder_1_out2));
  LED _3 (.in(decoder_1_out3));
endmodule
