// Logisim project Flip-flops.circ as structural Verilog: 1 circuit, main circuit main
module main (
  input  in_1,
  input  in_2,
  input  in_3,
  input  in_4,
  input  in_5,
  input  in_6
);

  wire clock_1_out, clock_2_out, clock_3_out, clock_4_out, d_ff_1_q, d_ff_1_qn, j_k_ff_1_q, j_k_ff_1_qn,
       s_r_ff_1_q, s_r_ff_1_qn, t_ff_1_q, t_ff_1_qn;

  Clock clock_1 (.out(clock_1_out));
  Clock clock_2 (.out(clock_2_out));
  Clock clock_3 (.out(clock_3_out));
  Clock clock_4 (.out(clock_4_out));
  S_R_Flip_Flop s_r_ff_1 (
    .S(in_1), .clk(clock_1_out), .R(in_2), .Q(s_r_ff_1_q), .Qn(s_r_ff_1_qn));  // open: preset, reset, en
  J_K_Flip_Flop j_k_ff_1 (
    .J(in_3), .clk(clock_2_out), .K(in_4), .Q(j_k_ff_1_q), .Qn(j_k_ff_1_qn));  // open: preset, en, reset
  D_Flip_Flop d_ff_1 (.clk(clock_3_out), .D(in_5), .Q(d_ff_1_q), .Qn(d_ff_1_qn));  // open: preset, en, reset
  LED led_1 (.in(s_r_ff_1_q));
  LED led_2 (.in(s_r_ff_1_qn));
  LED led_3 (.in(j_k_ff_1_q));
  LED led_4 (.in(j_k_ff_1_qn));
  LED led_5 (.in(d_ff_1_q));
  LED led_6 (.in(d_ff_1_qn));
  LED led_7 (.in(t_ff_1_q));
  T_Flip_Flop t_ff_1 (.clk(clock_4_out), .T(in_6), .Q(t_ff_1_q), .Qn(t_ff_1_qn));  // open: preset, reset, en
  LED led_8 (.in(t_ff_1_qn));
endmodule
