// Logisim project MUX 3bit.circ as structural Verilog: 1 circuit, main circuit main
module main (
  input  _0,
  input  _1,
  input  _2,
  input  _3,
  input  _4,
  input  _5,
  input  _6,
  input  in_8,
  input  _7,
  input  [2:0] in_10
);

  wire multiplexer_1_out;

  Multiplexer #(.select(3)) multiplexer_1 (
    .in0(_0), .in1(_1), .in2(_2), .in3(_3), .in4(_4), .in5(_5), .in6(_6), .in7(_7), .out(multiplexer_1_out),
    .sel(in_10), .en(in_8));
  LED led_1 (.in(multiplexer_1_out));
endmodule
