// Logisim project lab final.circ as structural Verilog: 1 circuit, main circuit main
module main (
  input  C,
  input  B,
  input  A,
  input  in_4
);

  wire and_1_out, and_2_out, and_3_out, and_4_out, and_5_out, clock_1_out, j_k_ff_1_q, j_k_ff_2_q,
       j_k_ff_3_q, j_k_ff_4_q, or_1_out, xor_1_out, xor_2_out;

  Clock clock_1 (.out(clock_1_out));
  LED Q4 (.in(j_k_ff_4_q));
  LED Q2 (.in(j_k_ff_3_q));
  xor xor_1 (xor_1_out, A, A);
  LED Q1 (.in(j_k_ff_2_q));
  LED Q0 (.in(j_k_ff_1_q));
  J_K_Flip_Flop j_k_ff_1 (
    .J(in_4), .clk(clock_1_out), .K(in_4), .Q(j_k_ff_1_q), .reset(and_4_out));  // open: Qn, preset, en
  and and_1 (and_1_out, xor_1_out, C);
  and and_2 (and_2_out, A, B);
  J_K_Flip_Flop j_k_ff_2 (
    .J(j_k_ff_1_q), .clk(clock_1_out), .K(j_k_ff_1_q), .Q(j_k_ff_2_q), .reset(and_4_out));  // open: Qn, preset, en
  and and_3 (and_3_out, j_k_ff_1_q, j_k_ff_2_q);
  and and_4 (and_4_out, j_k_ff_1_q, j_k_ff_2_q, j_k_ff_3_q, j_k_ff_4_q);
  xor xor_2 (xor_2_out, xor_1_out, C);
  or or_1 (or_1_out, and_1_out, and_2_out);
  and and_5 (and_5_out, and_3_out, j_k_ff_3_q);
  J_K_Flip_Flop j_k_ff_3 (
    .J(and_3_out), .clk(clock_1_out), .K(and_3_out), .Q(j_k_ff_3_q), .reset(and_4_out));  // open: Qn, preset, en
  LED S (.in(xor_2_out));
  LED u_C (.in(or_1_out));
  J_K_Flip_Flop j_k_ff_4 (
    .J(and_5_out), .clk(clock_1_out), .K(and_5_out), .Q(j_k_ff_4_q), .reset(and_4_out));  // open: Qn, preset, en
endmodule
