// Logisim project mod 10.circ as structural Verilog: 1 circuit, main circuit main
module main (
  input  in_1
);

  wire and_1_out, and_2_out, and_3_out, clock_1_out, j_k_ff_1_q, j_k_ff_2_q, j_k_ff_3_q, j_k_ff_4_q;

  Clock clock_1 (.out(clock_1_out));
  LED Q3 (.in(j_k_ff_4_q));
  LED Q2 (.in(j_k_ff_3_q));
  J_K_Flip_Flop j_k_ff_1 (
    .J(in_1), .clk(clock_1_out), .K(in_1), .Q(j_k_ff_1_q), .reset(and_2_out));  // open: Qn, preset, en
  LED Q1 (.in(j_k_ff_2_q));
  LED Q0 (.in(j_k_ff_1_q));
  and and_1 (and_1_out, j_k_ff_1_q, j_k_ff_2_q);
  J_K_Flip_Flop j_k_ff_2 (
    .J(j_k_ff_1_q), .clk(clock_1_out), .K(j_k_ff_1_q), .Q(j_k_ff_2_q), .reset(and_2_out));  // open: Qn, preset, en
  and and_2 (and_2_out, j_k_ff_4_q, j_k_ff_1_q);
  J_K_Flip_Flop j_k_ff_3 (
    .J(and_1_out), .clk(clock_1_out), .K(and_1_out), .Q(j_k_ff_3_q), .reset(and_2_out));  // open: Qn, preset, en
  and and_3 (and_3_out, and_1_out, j_k_ff_3_q);
  J_K_Flip_Flop j_k_ff_4 (
    .J(and_3_out), .clk(clock_1_out), .K(and_3_out), .Q(j_k_ff_4_q), .reset(and_2_out));  // open: Qn, preset, en
endmodule
