// Logisim project 2003055.circ as structural Verilog: 6 circuits, main circuit ORR
module ORR (
  input  [3:0] ORin,
  input  [3:0] ORin2,
  output [3:0] OROut
);

  assign OROut = ORin | ORin2;  // OR_Gate or_1, 4 bits wide
endmodule

module ADD (
  input  A,
  input  B,
  input  Cin,
  output SUM,
  output Carry
);

  wire and_1_out, and_2_out, xor_1_out;

  xor xor_1 (xor_1_out, A, B);
  and and_1 (and_1_out, A, B);
  and and_2 (and_2_out, Cin, xor_1_out);
  xor xor_2 (SUM, xor_1_out, Cin);
  or or_1 (Carry, and_2_out, and_1_out);
endmodule

module NotCircuit (
  input  [3:0] in_1,
  output [3:0] out_2
);

  assign out_2 = ~in_1;  // NOT_Gate not_1, 4 bits wide
endmodule

module FourBitAdd (
  input  CarryIn,
  input  [3:0] A,
  input  [3:0] B,
  output Carryout,
  output [3:0] SUM
);

  wire add_1_carry, add_2_carry, add_3_carry;

  ADD add_1 (.A(A[0]), .B(B[0]), .Cin(CarryIn), .SUM(SUM[0]), .Carry(add_1_carry));
  ADD add_2 (.A(A[1]), .B(B[1]), .Cin(add_1_carry), .SUM(SUM[1]), .Carry(add_2_carry));
  ADD add_3 (.A(A[2]), .B(B[2]), .Cin(add_2_carry), .SUM(SUM[2]), .Carry(add_3_carry));
  ADD add_4 (.A(A[3]), .B(B[3]), .Cin(add_3_carry), .SUM(SUM[3]), .Carry(Carryout));
endmodule

module LeftShift (
  input  [3:0] A,
  input  [1:0] Decider,
  output [3:0] Shift
);

  wire [3:0] shifter_1_out;

  Shifter #(.width(4)) shifter_1 (.in(A), .\dist (Decider), .out(shifter_1_out));
endmodule

module ALU (
  input  [3:0] in_1,
  input  [3:0] in_2,
  input  in_3,
  input  [3:0] in_4,
  input  [3:0] in_5,
  input  [3:0] in_6,
  input  [1:0] in_7,
  input  [3:0] in_8,
  input  [1:0] Sel,
  output [3:0] OutputALU,
  output CF
);

  wire fourbitadd_1_carryout;
  wire [3:0] fourbitadd_1_sum, leftshift_1_shift, multiplexer_1_out, notcircuit_1_out_2, orr_1_orout;

  ORR orr_1 (.ORin(in_1), .ORin2(in_2), .OROut(orr_1_orout));
  FourBitAdd fourbitadd_1 (
    .CarryIn(in_3), .A(in_4), .B(in_5), .Carryout(fourbitadd_1_carryout), .SUM(fourbitadd_1_sum));
  LeftShift leftshift_1 (.A(in_6), .Decider(in_7), .Shift(leftshift_1_shift));
  NotCircuit notcircuit_1 (.in_1(in_8), .out_2(notcircuit_1_out_2));
  Multiplexer #(.select(2), .width(4)) multiplexer_1 (
    .in0(orr_1_orout), .in1(fourbitadd_1_sum), .in2(leftshift_1_shift), .in3(notcircuit_1_out_2),
    .out(multiplexer_1_out), .sel(Sel));
endmodule
