// Logisim project LPE2_2003055.circ as structural Verilog: 3 circuits, main circuit OneBit
module OneBit (
  input  Din,
  input  SEL,
  input  CLK,
  output Dout
);

  wire multiplexer_1_out;

  Multiplexer multiplexer_1 (.in0(Dout), .in1(Din), .out(multiplexer_1_out), .sel(SEL));
  D_Flip_Flop d_ff_1 (.D(multiplexer_1_out), .clk(CLK), .Q(Dout));  // open: Qn, preset, reset
endmodule

module EightBit (
  input  [7:0] Din,
  input  SEL,
  input  CLK,
  output [7:0] Dout
);

  OneBit onebit_1 (.Din(Din[7]), .SEL(SEL), .CLK(CLK), .Dout(Dout[7]));
  OneBit onebit_2 (.Din(Din[6]), .SEL(SEL), .CLK(CLK), .Dout(Dout[6]));
  OneBit onebit_3 (.Din(Din[5]), .SEL(SEL), .CLK(CLK), .Dout(Dout[5]));
  OneBit onebit_4 (.Din(Din[4]), .SEL(SEL), .CLK(CLK), .Dout(Dout[4]));
  OneBit onebit_5 (.Din(Din[3]), .SEL(SEL), .CLK(CLK), .Dout(Dout[3]));
  OneBit onebit_6 (.Din(Din[2]), .SEL(SEL), .CLK(CLK), .Dout(Dout[2]));
  OneBit onebit_7 (.Din(Din[1]), .SEL(SEL), .CLK(CLK), .Dout(Dout[1]));
  OneBit onebit_8 (.Din(Din[0]), .SEL(SEL), .CLK(CLK), .Dout(Dout[0]));
endmodule

module Flag (
  input  CF,
  input  SF,
  input  ZF,
  input  CLK,
  output CF_2,
  output SF_2,
  output ZF_2
);

  OneBit onebit_1 (.Din(CF), .SEL(1'b1), .CLK(CLK), .Dout(CF_2));
  OneBit onebit_2 (.Din(SF), .SEL(1'b1), .CLK(CLK), .Dout(SF_2));
  OneBit onebit_3 (.Din(ZF), .SEL(1'b1), .CLK(CLK), .Dout(ZF_2));
endmodule
