// Logisim project Full_Adder.circ as structural Verilog
module main (
  input  A,
  input  B,
  input  Cin,
  output Sum,
  output Cout
);

  wire and_1_out, and_2_out, xor_1_out;

  xor xor_1 (xor_1_out, A, B);
  and and_1 (and_1_out, A, B);
  xor xor_2 (Sum, xor_1_out, Cin);
  and and_2 (and_2_out, xor_1_out, Cin);
  or or_1 (Cout, and_2_out, and_1_out);

  // Notes on the sheet:
  //   Full Adder Circuit
endmodule

module FA (
  input  A,
  input  B,
  input  Cin,
  output Sum,
  output Cout
);

  wire and_1_out, and_2_out, xor_1_out;

  xor xor_1 (xor_1_out, A, B);
  and and_1 (and_1_out, A, B);
  xor xor_2 (Sum, xor_1_out, Cin);
  and and_2 (and_2_out, xor_1_out, Cin);
  or or_1 (Cout, and_2_out, and_1_out);
endmodule

module F4bit (
  input  in_1,
  input  in_2,
  input  in_3,
  input  in_4,
  input  in_5,
  input  in_6,
  input  in_7,
  input  in_8,
  input  in_9,
  output out_10,
  output out_11,
  output out_12,
  output out_13,
  output out_14
);

  wire fa_1_cout, fa_2_cout, fa_3_cout;

  FA fa_1 (.A(in_2), .B(in_1), .Cin(in_9), .Sum(out_14), .Cout(fa_1_cout));
  FA fa_2 (.A(in_4), .B(in_3), .Cin(fa_1_cout), .Sum(out_13), .Cout(fa_2_cout));
  FA fa_3 (.A(in_6), .B(in_5), .Cin(fa_2_cout), .Sum(out_12), .Cout(fa_3_cout));
  FA fa_4 (.A(in_8), .B(in_7), .Cin(fa_3_cout), .Sum(out_11), .Cout(out_10));
endmodule

module FA4bitSIR (
  input  Cin,
  input  [3:0] in_2,
  input  [3:0] in_3,
  output Cout,
  output S3,
  output S2,
  output S1,
  output S0
);

  wire fa_1_cout, fa_2_cout, fa_3_cout;

  FA fa_1 (.A(in_2[0]), .B(in_3[0]), .Cin(Cin), .Sum(S0), .Cout(fa_1_cout));
  FA fa_2 (.A(in_2[1]), .B(in_3[1]), .Cin(fa_1_cout), .Sum(S1), .Cout(fa_2_cout));
  FA fa_3 (.A(in_2[2]), .B(in_3[2]), .Cin(fa_2_cout), .Sum(S2), .Cout(fa_3_cout));
  FA fa_4 (.A(in_2[3]), .B(in_3[3]), .Cin(fa_3_cout), .Sum(S3), .Cout(Cout));

  // Notes on the sheet:
  //   A
  //   B
  //   Four Bits Full Adder Circuit
endmodule
