// Logisim project eval.circ as structural Verilog: 2 circuits, main circuit main
module main (
  input  Din,
  input  SEL,
  input  CLK,
  output Dout
);

  wire multiplexer_1_out;

  Multiplexer multiplexer_1 (.in0(Dout), .in1(Din), .out(multiplexer_1_out), .sel(SEL));
  D_Flip_Flop d_ff_1 (.D(multiplexer_1_out), .clk(CLK), .Q(Dout));  // open: Qn, preset, reset
endmodule

module OnebitRegister (
);

  // main main_1: pin names not known
  // main main_2: pin names not known
  // main main_3: pin names not known
  // main main_4: pin names not known
endmodule
