// Logisim project p1.circ as structural Verilog: 5 circuits, main circuit fullA
module fullA (
  input  in_1,
  input  in_2,
  input  in_3,
  input  in_4,
  input  in_5
);

  wire and_1_out, and_2_out, xor_1_out;

  xor xor_1 (xor_1_out, in_1, in_3);
  and and_1 (and_1_out, in_1, in_3);
  xor xor_2 (in_2, xor_1_out, in_4);
  and and_2 (and_2_out, xor_1_out, in_4);
  or or_1 (in_5, and_2_out, and_1_out);
endmodule

module FourBitAdder (
  input  [3:0] A,
  input  [3:0] B,
  input  in_3
);

  wire fulladder_1_s;

  fulladder fulladder_1 (.A(A[0]), .B(B[3]), .Cin(in_3), .S(fulladder_1_s), .Cout(fulladder_1_s));
  fulladder fulladder_2 (.Cin(fulladder_1_s));  // open: A, B, S, Cout
  fulladder fulladder_3 ();  // open: A, B, Cin, S, Cout
  fulladder fulladder_4 ();  // open: A, B, Cin, S, Cout
endmodule

module fulladder (
  input  A,
  input  B,
  input  Cin,
  output S,
  output Cout
);

  wire and_1_out, and_2_out, xor_1_out;

  xor xor_1 (xor_1_out, A, B);
  and and_1 (and_1_out, A, B);
  xor xor_2 (S, xor_1_out, Cin);
  and and_2 (and_2_out, xor_1_out, Cin);
  or or_1 (Cout, and_2_out, and_1_out);
endmodule

module Nmos_Proje (
  input  in_1,
  input  in_2,
  input  in_3,
  input  in_4,
  output out_5,
  output out_6
);

  wire transistor_4_out;

  Transistor #(.\type ("n")) transistor_1 (.in(1'b0), .out(out_5), .gate(in_1));
  Pull_Resistor #(.pull(1)) pull_resistor_1 (.node(out_5));
  Transistor #(.\type ("n")) transistor_2 (.in(1'b0), .out(out_5), .gate(in_2));
  Pull_Resistor #(.pull(1)) pull_resistor_2 (.node(out_6));
  Transistor #(.\type ("n")) transistor_3 (.in(transistor_4_out), .out(out_6), .gate(in_3));
  Transistor #(.\type ("n")) transistor_4 (.in(1'b0), .out(transistor_4_out), .gate(in_4));
endmodule

module decoder_2_4 (
  input  [1:0] in_1,
  input  in_2,
  output out_3,
  output out_4,
  output out_5,
  output out_6
);

  Decoder #(.select(2)) decoder_1 (.out0(out_3), .out1(out_4), .out2(out_5), .out3(out_6), .sel(in_1), .en(in_2));
endmodule
